// Logisim project Project2.circ as structural Verilog: 13 circuits, main circuit main
module main (
);

  wire ALUop, ALUsrc, clock, MemRead, MemToReg, MemWrite, Reg2Lock, RegWrite;
  wire [1:0] d, m, n, ReadReg2, t;
  wire [7:0] ALU_outputofaddorsub, DataMemory_readdata, imm, middlemux_1_inputb, MUXonbottom_regdataw,
       pc_1_pcout, pcaddercircuit_1_nextpc, RegisterFile_regdata1, RegisterFile_regdata2;

  PCadderCircuit pcaddercircuit_1 (.PCAdderInput(pc_1_pcout), .nextPC(pcaddercircuit_1_nextpc));
  AddOrSub ALU (
    .inputA(RegisterFile_regdata1), .InputB(middlemux_1_inputb), .Choice(ALUop),
    .OutputOfAddOrSub(ALU_outputofaddorsub));  // open: Z
  Clock clock_1 (.out(clock));
  PC pc_1 (.InputFromMUX(pcaddercircuit_1_nextpc), .clock(clock), .PCout(pc_1_pcout));
  memory DataMemory (
    .Address(ALU_outputofaddorsub), .memWrite(MemWrite), .WriteData(RegisterFile_regdata2),
    .memRead(MemRead), .clock(clock), .readData(DataMemory_readdata));
  complexMUX1 MUXonbottom (
    .ALUoutput(ALU_outputofaddorsub), .readData(DataMemory_readdata), .MemToReg(MemToReg),
    .RegDataW(MUXonbottom_regdataw));
  Address address_1 (
    .PCOutput(pc_1_pcout), .clock(clock),
    .I({Reg2Lock, ALUop, RegWrite, ALUsrc, MemRead, MemWrite, MemToReg, d, t, m, n, imm}));
  finalTopMUX finaltopmux_1 (.m(m), .t(t), .reg2Loc(Reg2Lock), .ReadReg2(ReadReg2));
  middleMUX middlemux_1 (.RegData2(RegisterFile_regdata2), .imm(imm), .ALUsrc(ALUsrc), .inputB(middlemux_1_inputb));
  lab8 RegisterFile (
    .ReadReg1(n), .WriteReg(d), .RegWrite(RegWrite), .RegDataW(MUXonbottom_regdataw), .ReadReg2(ReadReg2),
    .RegData1(RegisterFile_regdata1), .RegData2(RegisterFile_regdata2));

  // Notes on the sheet:
  //   LDR(Rd, Rn, imm)
  //   STR(Rm, Rn, imm)
  //   ADD
  //   SUB
  //   0011101[Rd]0000[Rn][imm8]
  //   00010100000[Rm][Rn][imm8]
  //   0011100[Rd]0000[Rn][imm8]
  //   0111100[Rd]0000[Rn][imm8]
endmodule

module lab8 (
  input  [1:0] ReadReg1,
  input  [1:0] WriteReg,
  input  RegWrite,
  input  [7:0] RegDataW,
  input  [1:0] ReadReg2,
  output [7:0] RegData1,
  output [7:0] RegData2
);

  wire and_1_out, and_2_out, and_3_out, and_4_out, clock_1_out, decoder_1_out0, decoder_1_out1,
       decoder_1_out2, decoder_1_out3;
  wire [7:0] X0_q, X1_q, X2_q, X3_q;

  Clock clock_1 (.out(clock_1_out));
  Decoder #(.enable("false"), .select(2)) decoder_1 (
    .out0(decoder_1_out0), .out1(decoder_1_out1), .out2(decoder_1_out2), .out3(decoder_1_out3), .sel(WriteReg));
  and and_1 (and_1_out, decoder_1_out0, RegWrite);
  and and_2 (and_2_out, RegWrite, decoder_1_out1);
  and and_3 (and_3_out, decoder_1_out2, RegWrite);
  and and_4 (and_4_out, RegWrite, decoder_1_out3);
  Register X0 (.D(RegDataW), .en(and_1_out), .clk(clock_1_out), .Q(X0_q));  // open: clr
  Register X1 (.D(RegDataW), .en(and_2_out), .clk(clock_1_out), .Q(X1_q));  // open: clr
  Register X2 (.D(RegDataW), .en(and_3_out), .clk(clock_1_out), .Q(X2_q));  // open: clr
  Register X3 (.D(RegDataW), .en(and_4_out), .clk(clock_1_out), .Q(X3_q));  // open: clr
  Multiplexer #(.select(2), .width(8)) multiplexer_1 (
    .in0(X0_q), .in1(X1_q), .in2(X2_q), .in3(X3_q), .out(RegData1), .sel(ReadReg1));
  Multiplexer #(.select(2), .width(8)) multiplexer_2 (
    .in0(X0_q), .in1(X1_q), .in2(X2_q), .in3(X3_q), .out(RegData2), .sel(ReadReg2));
endmodule

module AddOrSub (
  input  [7:0] inputA,
  input  [7:0] InputB,
  input  Choice,
  output Z,
  output [7:0] OutputOfAddOrSub
);

  wire [7:0] adder_1_out, subtractor_1_out;

  Adder adder_1 (.a(inputA), .b(InputB), .out(adder_1_out));  // open: cin, cout
  Subtractor subtractor_1 (.a(inputA), .b(InputB), .out(subtractor_1_out));  // open: bin, bout
  Multiplexer #(.width(8)) multiplexer_1 (
    .in0(adder_1_out), .in1(subtractor_1_out), .out(OutputOfAddOrSub), .sel(Choice));
  Comparator comparator_1 (.a({8{1'b0}}), .b(OutputOfAddOrSub), .eq(Z));  // open: gt, lt
endmodule

module memory (
  input  [7:0] Address,
  input  memWrite,
  input  [7:0] WriteData,
  input  memRead,
  input  clock,
  output [7:0] readData
);

  RAM #(.asyncread("true")) ram_1 (
    .addr(Address), .we(memWrite), .oe(memRead), .clk(clock), .din(WriteData), .dout(readData));
endmodule

module complexMUX1 (
  input  [7:0] ALUoutput,
  input  [7:0] readData,
  input  MemToReg,
  output [7:0] RegDataW
);

  Multiplexer #(.width(8)) multiplexer_1 (.in0(ALUoutput), .in1(readData), .out(RegDataW), .sel(MemToReg));
endmodule

module PCadderCircuit (
  input  [7:0] PCAdderInput,
  output [7:0] nextPC
);

  Adder adder_1 (.a(8'h1), .b(PCAdderInput), .out(nextPC));  // open: cin, cout
endmodule

module PC (
  input  [7:0] InputFromMUX,
  input  clock,
  output [7:0] PCout
);

  Register register_1 (.D(InputFromMUX), .en(1'b1), .clk(clock), .Q(PCout));  // open: clr
endmodule

module Address (
  input  [7:0] PCOutput,
  input  clock,
  output [22:0] I
);

  RAM #(.dataWidth(23), .enables("line")) ram_1 (
    .addr(PCOutput), .we(1'b0), .oe(1'b0), .clk(clock), .dout(I));  // open: din

  // Notes on the sheet:
  //   LDR(Rd, Rn, imm)
  //   STR(Rn, Rm, imm)
  //   ADD(Rd, Rn, imm)
  //   SUB(Rd, Rn, imm)
  //   0011101[Rd]0000[Rn][imm8]
  //   00010100000[Rm][Rn][imm8]
  //   0011100[Rd]0000[Rn][imm8]
  //   0111100[Rd]0000[Rn][imm8]
endmodule

module BrPc (
  input  [7:0] IOutput,
  input  [7:0] PCoutput,
  output [7:0] BrPCOUT
);

  Adder adder_1 (.a(IOutput), .b(PCoutput), .out(BrPCOUT));  // open: cin, cout
endmodule

module ComplexMUXPC (
  input  [7:0] NextPC,
  input  [7:0] ALUOut,
  input  [7:0] BrPCOut,
  input  PBr,
  input  Br,
  output [7:0] ToPC
);

  wire [7:0] multiplexer_1_out;

  Multiplexer #(.width(8)) multiplexer_1 (.in0(NextPC), .in1(ALUOut), .out(multiplexer_1_out), .sel(PBr));
  Multiplexer #(.width(8)) multiplexer_2 (.in0(multiplexer_1_out), .in1(BrPCOut), .out(ToPC), .sel(Br));
endmodule

module I (
  output ToBrPC
);
endmodule

module finalTopMUX (
  input  [1:0] m,
  input  [1:0] t,
  input  reg2Loc,
  output [1:0] ReadReg2
);

  Multiplexer #(.width(2)) multiplexer_1 (.in0(m), .in1(t), .out(ReadReg2), .sel(reg2Loc));
endmodule

module middleMUX (
  input  [7:0] RegData2,
  input  [7:0] imm,
  input  ALUsrc,
  output [7:0] inputB
);

  Multiplexer #(.width(8)) multiplexer_1 (.in0(RegData2), .in1(imm), .out(inputB), .sel(ALUsrc));
endmodule
